// Logisim project smips.circ as structural Verilog
module Board (
);

  wire CLK, HALT, MEM_WE, RESET, TTY_WE;
  wire [3:0] MEM_BE;
  wire [6:0] TTY_DATA;
  wire [31:0] MEM_ADDR, MEM_RDATA, MEM_WDATA;

  Clock Reloj (.out(CLK));
  Button u_Reset (.out(RESET));
  CPU cpu_1 (
    .CLK(CLK), .RESET(RESET), .MEM_RDATA(MEM_RDATA), .MEM_ADDR(MEM_ADDR), .MEM_WDATA(MEM_WDATA),
    .MEM_BE(MEM_BE), .MEM_WE(MEM_WE), .TTY_DATA(TTY_DATA), .TTY_WE(TTY_WE), .HALT(HALT));
  TTY #(.cols(48), .rows(12)) tty_1 (.data(TTY_DATA), .clk(CLK), .we(TTY_WE), .clr(RESET));
  Memory memory_1 (.CLK(CLK), .ADDR(MEM_ADDR), .WDATA(MEM_WDATA), .BE(MEM_BE), .WE(MEM_WE), .RDATA(MEM_RDATA));
  LED u_Halt (.in(HALT));

  // Notes on the sheet:
  //   S-MIPS | Board
  //   No modificar: la CPU se implementa dentro del subcircuito CPU.
endmodule

module CPU (
  input  CLK,
  input  RESET,
  input  [31:0] MEM_RDATA,
  output [31:0] MEM_ADDR,
  output [31:0] MEM_WDATA,
  output [3:0] MEM_BE,
  output MEM_WE,
  output [6:0] TTY_DATA,
  output TTY_WE,
  output HALT
);

  Instruction_Decoder instruction_decoder_1 ();  // open: Funct, Op, IMM_MODE, Is_R, Is_Syscall, Is_Load, Is_Store, ALU_OP, ILLEGAL, Is_Branch, Is_Jump
  Datapath datapath_1 ();  // open: ALU_OP, in_2, Shamt, ALUSrcA_SEL, ALUSrcB_SEL, WRITE_BACK, in_7, in_8, in_9, MEM_RDATA, RegWrite, PC_OUT, MEM_WDATA, MEM_ADDR, MEM_BE, BR_EQ
  Branch_Control branch_control_1 ();  // open: Bne, Op1, Beq, Op2, Branch_Taken

  // Notes on the sheet:
  //   CPU S-MIPS: implementar aqui
  //   No cambiar nombres, anchos ni sentido de los pines: la placa depende de ellos.
endmodule

module Memory (
  input  CLK,
  input  [31:0] ADDR,
  input  [31:0] WDATA,
  input  [3:0] BE,
  input  WE,
  output [31:0] RDATA
);

  RAM #(.addrWidth(12), .asyncread("true"), .byteenables("byteEnables"), .dataWidth(32), .\type ("nonvolatile")) Main_Memory (
    .addr(ADDR[13:2]), .we(WE), .oe(1'b1), .clk(CLK), .din(WDATA), .dout(RDATA), .be3(BE[3]), .be2(BE[2]),
    .be1(BE[1]), .be0(BE[0]));

  // Other names for the same wires on the sheet: A[11:0] = ADDR[13:2]

  // Notes on the sheet:
  //   Memoria unificada: 4096 palabras de 32 bits (16 KiB), little-endian
  //   Lectura combinacional; escritura en el flanco de subida de CLK con WE=1, solo en los bytes con BE=1.
  //   Se usan los bits 13..2 de ADDR; los demas se ignoran (el espacio se repite cada 16 KiB).
endmodule

module Datapath (
  input  [2:0] ALU_OP,
  input  in_2,
  input  [4:0] Shamt,
  input  [1:0] ALUSrcA_SEL,
  input  [1:0] ALUSrcB_SEL,
  input  [31:0] WRITE_BACK,
  input  in_7,
  input  in_8,
  input  in_9,
  input  [31:0] MEM_RDATA,
  input  RegWrite,
  output [31:0] PC_OUT,
  output [31:0] MEM_WDATA,
  output [31:0] MEM_ADDR,
  output [3:0] MEM_BE,
  output BR_EQ
);

  wire CLK;
  wire [1:0] undriven;
  wire [15:0] Imm16;
  wire [31:0] A_q, alu_1_result, ALUOUT, B_q, bit_extender_1_out, bit_extender_2_out, IR_OUT, MDROUT,
       multiplexer_1_out, multiplexer_3_out, multiplexer_4_out, register_file_1_read_data1,
       register_file_1_read_data2;

  Clock clock_1 (.out(CLK));
  Register #(.width(32)) IR (.en(in_8), .clk(CLK), .Q(IR_OUT), .clr(in_2));  // open: D
  Register #(.width(32)) MDR (.D(MEM_RDATA), .clk(CLK), .Q(MDROUT));  // open: en, clr
  Register_File register_file_1 (
    .WRITE_DATA(WRITE_BACK), .READ_DATA1(register_file_1_read_data1), .READ_DATA2(register_file_1_read_data2));  // open: CLK, RESET, REG_WRITE, READ_ADDR1, READ_ADDR2, WRITE_ADDR
  Register #(.width(32)) A (.D(register_file_1_read_data1), .en(1'b1), .clk(CLK), .Q(A_q));  // open: clr
  Register #(.width(32)) B (.D(register_file_1_read_data2), .en(1'b1), .clk(CLK), .Q(B_q));  // open: clr
  Multiplexer #(.select(2), .width(32)) multiplexer_1 (
    .in3(ALUOUT), .out(multiplexer_1_out), .sel(undriven));  // open: in0, in1, in2
  Register #(.width(32)) PC (.D(multiplexer_1_out), .en(in_9), .clk(CLK), .Q(PC_OUT), .clr(in_2));
  Multiplexer #(.width(32)) multiplexer_2 (.in0(ALUOUT), .in1(MDROUT), .out(WRITE_BACK));  // open: sel
  assign bit_extender_1_out = {{27{Shamt[4]}}, Shamt};  // Bit_Extender bit_extender_1
  assign bit_extender_2_out = {{16{Imm16[15]}}, Imm16};  // Bit_Extender bit_extender_2
  Bit_Extender #(.in_width(16), .out_width(32), .\type ("zero")) bit_extender_3 (.in(Imm16));  // open: out
  Multiplexer #(.select(2), .width(32)) multiplexer_3 (
    .in0(PC_OUT), .in1(A_q), .in2(bit_extender_1_out), .out(multiplexer_3_out), .sel(ALUSrcA_SEL));  // open: in3
  Multiplexer #(.select(2), .width(32)) multiplexer_4 (
    .in0(B_q), .in1(32'h4), .in2(bit_extender_2_out), .out(multiplexer_4_out), .sel(ALUSrcB_SEL));  // open: in3
  Shifter #(.width(32)) shifter_1 (.in(bit_extender_2_out), .\dist (5'b00010));  // open: out
  ALU alu_1 (.A(multiplexer_3_out), .B(multiplexer_4_out), .ALU_OP(ALU_OP), .RESULT(alu_1_result), .ZERO(in_7));
  Register #(.width(32)) u_ALUOUT (.D(alu_1_result), .clk(CLK), .Q(ALUOUT));  // open: en, clr

  // Other names for the same wires on the sheet: IRWrite = in_8; PCWrite = in_9; RESET = in_2; ZERO = in_7

  // Notes on the sheet:
  //   ALUSrcA
  //   ALUSrcB
  //   INPUTS/OUTPUTS
endmodule

module Instruction_Decoder (
  input  [5:0] Funct,
  input  [5:0] Op,
  output [1:0] IMM_MODE,
  output Is_R,
  output Is_Syscall,
  output Is_Load,
  output Is_Store,
  output [2:0] ALU_OP,
  output ILLEGAL,
  output Is_Branch,
  output Is_Jump
);

  wire comparator_1_eq, comparator_2_eq, comparator_3_eq, comparator_4_eq, comparator_5_eq, comparator_6_eq,
       comparator_7_eq, comparator_8_eq, comparator_9_eq, comparator_10_eq, comparator_11_eq,
       comparator_12_eq, comparator_13_eq, comparator_14_eq, comparator_15_eq, comparator_16_eq,
       comparator_18_eq, comparator_19_eq, comparator_22_eq, comparator_23_eq, I_ADD, I_AND, I_LUI, I_OR,
       I_SLT, or_5_out, R_ADD, R_AND, R_OR, R_SLL, R_SLT, R_SRL, R_SUB;

  Comparator #(.width(6)) comparator_1 (.a(Funct), .b(6'b001100), .eq(comparator_1_eq));  // open: gt, lt
  Comparator #(.width(6)) comparator_2 (.a(Op), .b(6'b100011), .eq(comparator_2_eq));  // open: gt, lt
  Comparator #(.width(6)) comparator_3 (.a(Op), .b(6'b100000), .eq(comparator_3_eq));  // open: gt, lt
  Comparator #(.width(6)) comparator_4 (.a(Op), .b(6'b100100), .eq(comparator_4_eq));  // open: gt, lt
  Comparator #(.width(6)) comparator_5 (.a(Op), .b(6'b101011), .eq(comparator_5_eq));  // open: gt, lt
  Comparator #(.width(6)) comparator_6 (.a(Op), .b(6'b101000), .eq(comparator_6_eq));  // open: gt, lt
  Comparator #(.width(6)) comparator_7 (.a(Op), .b(6'b000100), .eq(comparator_7_eq));  // open: gt, lt
  Comparator #(.width(6)) comparator_8 (.a(Op), .b(6'b000101), .eq(comparator_8_eq));  // open: gt, lt
  Comparator #(.width(6)) comparator_9 (.a(Op), .b(6'b000010), .eq(comparator_9_eq));  // open: gt, lt
  Comparator #(.width(6)) comparator_10 (.a(Op), .b(6'b000011), .eq(comparator_10_eq));  // open: gt, lt
  nor nor_1 (Is_R, Op[0], Op[1], Op[2], Op[4], Op[5]);
  and and_1 (Is_Syscall, comparator_1_eq, Is_R);
  or or_1 (Is_Store, comparator_5_eq, comparator_6_eq);
  or or_2 (Is_Branch, comparator_7_eq, comparator_8_eq);
  or or_3 (Is_Jump, comparator_9_eq, comparator_10_eq);
  or or_4 (Is_Load, comparator_2_eq, comparator_3_eq, comparator_4_eq);
  Comparator #(.width(6)) comparator_11 (.a(Funct), .b(6'b100000), .eq(comparator_11_eq));  // open: gt, lt
  Comparator #(.width(6)) comparator_12 (.a(Funct), .b(6'b001100), .eq(comparator_12_eq));  // open: gt, lt
  Comparator #(.width(6)) comparator_13 (.a(Funct), .b(6'b100010), .eq(comparator_13_eq));  // open: gt, lt
  Comparator #(.width(6)) comparator_14 (.a(Funct), .b(6'b100100), .eq(comparator_14_eq));  // open: gt, lt
  Comparator #(.width(6)) comparator_15 (.a(Funct), .b({6{1'b0}}), .eq(comparator_15_eq));  // open: gt, lt
  Comparator #(.width(6)) comparator_16 (.a(Funct), .b(6'b000010), .eq(comparator_16_eq));  // open: gt, lt
  Comparator #(.width(6)) comparator_17 (.a(Op), .b(6'b001100), .eq(I_AND));  // open: gt, lt
  or or_5 (or_5_out, comparator_11_eq, comparator_12_eq);
  Comparator #(.width(6)) comparator_18 (.a(Funct), .b(6'b100101), .eq(comparator_18_eq));  // open: gt, lt
  Comparator #(.width(6)) comparator_19 (.a(Funct), .b(6'b101010), .eq(comparator_19_eq));  // open: gt, lt
  and and_2 (R_SLL, comparator_15_eq, Is_R);
  and and_3 (R_SRL, comparator_16_eq, Is_R);
  and and_4 (R_ADD, or_5_out, Is_R);
  and and_5 (R_SUB, comparator_13_eq, Is_R);
  and and_6 (R_AND, comparator_14_eq, Is_R);
  and and_7 (R_OR, comparator_18_eq, Is_R);
  and and_8 (R_SLT, comparator_19_eq, Is_R);
  Comparator #(.width(6)) comparator_20 (.a(Op), .b(6'b001101), .eq(I_OR));  // open: gt, lt
  Comparator #(.width(6)) comparator_21 (.a(Op), .b(6'b001010), .eq(I_SLT));  // open: gt, lt
  Comparator #(.width(6)) comparator_22 (.a(Op), .b(6'b001000), .eq(comparator_22_eq));  // open: gt, lt
  Comparator #(.width(6)) comparator_23 (.a(Op), .b(6'b001001), .eq(comparator_23_eq));  // open: gt, lt
  or or_6 (I_ADD, comparator_22_eq, comparator_23_eq);
  Comparator #(.width(6)) comparator_24 (.a(Op), .b(6'b001111), .eq(I_LUI));  // open: gt, lt

  // Other names for the same wires on the sheet: IMM_ZERO = IMM_MODE[0]; IMM_LUI = IMM_MODE[1]; OP_ZERO = Is_R
endmodule

module Branch_Control (
  input  Bne,
  input  [31:0] Op1,
  input  Beq,
  input  [31:0] Op2,
  output Branch_Taken
);

  wire and_1_out, and_2_out, comparator_1_eq, not_1_out;

  Comparator #(.width(32)) comparator_1 (.a(Op1), .b(Op2), .eq(comparator_1_eq));  // open: gt, lt
  not not_1 (not_1_out, comparator_1_eq);
  and and_1 (and_1_out, comparator_1_eq, Beq);
  and and_2 (and_2_out, Bne, not_1_out);
  or or_1 (Branch_Taken, and_2_out, and_1_out);
endmodule

// VHDL entity Register_File, as the project stores it:
library ieee;
use ieee.std_logic_1164.all;
use ieee.numeric_std.all;

entity Register_File is
    port (
        -- Control y sincronizacion
        CLK        : in  std_logic;
        RESET      : in  std_logic;
        REG_WRITE  : in  std_logic;

        -- Puerto de Lectura 1
        READ_ADDR1 : in  std_logic_vector(4 downto 0);
        READ_DATA1 : out std_logic_vector(31 downto 0);

        -- Puerto de Lectura 2
        READ_ADDR2 : in  std_logic_vector(4 downto 0);
        READ_DATA2 : out std_logic_vector(31 downto 0);

        -- Puerto de Escritura
        WRITE_ADDR : in  std_logic_vector(4 downto 0);
        WRITE_DATA : in  std_logic_vector(31 downto 0)
    );
end entity Register_File;

architecture RTL of Register_File is

    -- Array de 31 registros de 32 bits (el registro 0 se maneja de forma especial)
    type register_array is array (1 to 31) of std_logic_vector(31 downto 0);
    signal registers : register_array := (others => (others => '0'));

begin

    -- Proceso secuencial: Escritura sincrona y reset (R6)
    process (CLK)
    begin
        if rising_edge(CLK) then
            if RESET = '1' then
                registers     <= (others => (others => '0'));
                registers(28) <= x"00001800"; -- $gp inicial
                registers(29) <= x"00003FFC"; -- $sp inicial
            elsif REG_WRITE = '1' then
                if unsigned(WRITE_ADDR) /= 0 then
                    registers(to_integer(unsigned(WRITE_ADDR))) <= WRITE_DATA;
                end if;
            end if;
        end if;
    end process;

    -- Puerto de Lectura 1: Combinacional con proteccion estricta para $zero
    process (READ_ADDR1, registers)
    begin
        if unsigned(READ_ADDR1) = 0 then
            READ_DATA1 <= (others => '0');
        else
            READ_DATA1 <= registers(to_integer(unsigned(READ_ADDR1)));
        end if;
    end process;

    -- Puerto de Lectura 2: Combinacional con proteccion estricta para $zero
    process (READ_ADDR2, registers)
    begin
        if unsigned(READ_ADDR2) = 0 then
            READ_DATA2 <= (others => '0');
        else
            READ_DATA2 <= registers(to_integer(unsigned(READ_ADDR2)));
        end if;
    end process;

end architecture RTL;

// VHDL entity ALU, as the project stores it:
library ieee;
use ieee.std_logic_1164.all;
use ieee.numeric_std.all;

entity ALU is
    port (
        A       : in  std_logic_vector(31 downto 0);
        B       : in  std_logic_vector(31 downto 0);
        ALU_OP  : in  std_logic_vector(2 downto 0);
        RESULT  : out std_logic_vector(31 downto 0);
        ZERO    : out std_logic
    );
end entity ALU;

architecture RTL of ALU is

    signal res_internal : std_logic_vector(31 downto 0);

begin

    process (A, B, ALU_OP)
        variable signed_a   : signed(31 downto 0);
        variable signed_b   : signed(31 downto 0);
        variable unsigned_b : unsigned(31 downto 0);
        variable shift_amt  : integer range 0 to 31;
    begin

        signed_a   := signed(A);
        signed_b   := signed(B);
        unsigned_b := unsigned(B);
        shift_amt  := to_integer(unsigned(A(4 downto 0)));

        case ALU_OP is

            when "000" =>
                res_internal <= std_logic_vector(signed_a + signed_b);

            when "001" =>
                res_internal <= std_logic_vector(signed_a - signed_b);

            when "010" =>
                res_internal <= A and B;

            when "011" =>
                res_internal <= A or B;

            when "100" =>
                if signed_a < signed_b then
                    res_internal <= x"00000001";
                else
                    res_internal <= x"00000000";
                end if;

            when "101" =>
                res_internal <= std_logic_vector(
                    shift_left(unsigned_b, shift_amt)
                );

            when "110" =>
                res_internal <= std_logic_vector(
                    shift_right(unsigned_b, shift_amt)
                );

            when others =>
                res_internal <= (others => '0');

        end case;

    end process;

    RESULT <= res_internal;

    ZERO <= '1' when res_internal = x"00000000" else '0';

end architecture RTL;
